# Fritzing sketch Knight-Rider (saved by Fritzing 0.9.2b)
circuit board: 9.72021cm x 5.85373cm
breadboards: 1

parts:
  LED1 = LED - 5mm [color="Red (633nm)" package="5 mm [THT]"]
  LED2 = LED - 5mm [color="Red (633nm)" package="5 mm [THT]"]
  LED1_2 = LED - 5mm [color="Red (633nm)" package="5 mm [THT]"]
  LED2_2 = LED - 5mm [color="Red (633nm)" package="5 mm [THT]"]
  LED6 = LED - 5mm [color="Red (633nm)" package="5 mm [THT]"]
  LED7 = LED - 5mm [color="Red (633nm)" package="5 mm [THT]"]
  L8 = LED - 5mm [color="Red (633nm)" package="5 mm [THT]"]
  LED9 = LED - 5mm [color="Red (633nm)" package="5 mm [THT]"]
  LED10 = LED - 5mm [color="Red (633nm)" package="5 mm [THT]"]
  LED11 = LED - 5mm [color="Red (633nm)" package="5 mm [THT]"]
  LED12 = LED - 5mm [color="Red (633nm)" package="5 mm [THT]"]
  LED13 = LED - 5mm [color="Red (633nm)" package="5 mm [THT]"]
  R1 = Resistor [tolerance=±5% resistance=1k package=THT]
  R2 = Resistor [tolerance=±5% resistance=1k package=THT]
  R3 = Resistor [tolerance=±5% resistance=1k package=THT]
  R4 = Resistor [tolerance=±5% resistance=1k package=THT]
  R5 = Resistor [tolerance=±5% resistance=1k package=THT]
  R6 = Resistor [tolerance=±5% resistance=1k package=THT]
  R7 = Resistor [tolerance=±5% resistance=1k package=THT]
  R8 = Resistor [tolerance=±5% resistance=1k package=THT]
  R9 = Resistor [tolerance=±5% resistance=1k package=THT]
  R13 = Resistor [tolerance=±5% resistance=1k package=THT]
  R14 = Resistor [tolerance=±5% resistance=1k package=THT]
  R15 = Resistor [tolerance=±5% resistance=1k package=THT]
  Micro_Controller = Arduino Pro Mini v13
  POT = TRIMPOT [package=trimpot-5mm]

nets:
  N1: LED1.cathode, LED2.cathode, LED1_2.cathode, LED2_2.cathode, LED6.cathode, LED7.cathode, L8.cathode, LED9.cathode, LED10.cathode, LED11.cathode, LED12.cathode, LED13.cathode, Micro_Controller.GND, POT.CW
  N2: LED1.anode, R13.Pin_0
  N3: LED2.anode, R1.Pin_0
  N4: LED1_2.anode, R9.Pin_0
  N5: LED2_2.anode, R8.Pin_0
  N6: LED6.anode, R14.Pin_0
  N7: LED7.anode, R7.Pin_0
  N8: L8.anode, R6.Pin_0
  N9: LED9.anode, R5.Pin_0
  N10: LED10.anode, R4.Pin_0
  N11: LED11.anode, R3.Pin_0
  N12: LED12.anode, R2.Pin_0
  N13: LED13.anode, R15.Pin_0
  N14: R1.Pin_1, Micro_Controller.D4
  N15: R2.Pin_1, Micro_Controller.D6_PWM
  N16: R3.Pin_1, Micro_Controller.D7
  N17: R4.Pin_1, Micro_Controller.D8
  N18: R5.Pin_1, Micro_Controller.D9_PWM
  N19: R6.Pin_1, Micro_Controller.D10_PWM/SS
  N20: R7.Pin_1, Micro_Controller.D11_PWM/MOSI
  N21: R8.Pin_1, Micro_Controller.D12/MISO
  N22: R9.Pin_1, Micro_Controller.D13/SCK
  N23: R13.Pin_1, Micro_Controller.D2
  N24: R14.Pin_1, Micro_Controller.D3_PWM
  N25: R15.Pin_1, Micro_Controller.D5_PWM
  N26: Micro_Controller.VCC, POT.CCW
  N27: Micro_Controller.A3, POT.WIPER
